# Fritzing sketch Mibeat-Fritzing (saved by Fritzing 0.9.3b)
circuit board: 5.38524cm x 2.94515cm
breadboards: 1

parts:
  Part1 = Adafruit ADS1015 12Bit I2C ADC [part_number="Adafruit #1083"]
  JP1 = Header 4 [package=molex-1x4_lock]
  U1 = AVR 10-pin ICSP Header [package="avr icsp"]

nets:
  N1: Part1.SDA, JP1.1, U1.3
  N2: Part1.SCL, JP1.2, U1.5
  N3: Part1.GND, JP1.3, U1.9
  N4: Part1.VDD, JP1.4, U1.1

custom parts:
  Adafruit ADS1015 12Bit I2C ADC: For microcontrollers without an analog-to-digital converter or when you want a higher-precision ADC, the ADS1015 provides 12-bit precision at 3300 samples/second over I2C. The chip can be configured as 4 single-ended input channels, or two differential channels. As a nice bonus, it even includes a programmable gain amplifier, up to x16, to help boost up smaller single/differential signals to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
